# Fritzing sketch lamp (saved by Fritzing 0.9.0b)
circuit board: 8.46667cm x 5.64444cm
perfboards: 1

parts:
  S1 = Pushbutton [package="[THT]"]
  S2 = Pushbutton [package="[THT]"]
  J1 = female pin header, 2 pins [form="♀ (female)"]
  J2 = female pin header, 2 pins [form="♀ (female)"]
  J3 = female pin header, 2 pins [form="♀ (female)"]
  J4 = female pin header, 2 pins [form="♀ (female)"]
  JP1 = Header 3 [package=molex-1x3_lock]
  R1 = Resistor [tolerance=±5% resistance=220 package=THT]
  J5 = Power Jack [package=power_jack_combo]
  R2 = Resistor [tolerance=±5% resistance=220 package=THT]
  Part1 = Arduino Uno (Rev3)
  U2 = Voltage Regulator - 3.3V [package="TO220 [THT]"]

nets:
  N1: S1.Pin_1, S1.Pin_2, R2.Pin_0, Part1.D3_PWM
  GND: S1.Pin_3, S1.Pin_4, S2.Pin_1, S2.Pin_2, J2.pin2, JP1.3, J5.GND, Part1.GND, U2.GND
  N2: S2.Pin_3, S2.Pin_4, R1.Pin_0, Part1.D2
  N3: J1.pin1, Part1.D1/TX
  N4: J3.pin1, J4.pin1, U2.output_voltage
  N5: J4.pin2, Part1.D0/RX
  N6: JP1.1, Part1.D11_PWM/MOSI
  N7: JP1.2, R1.Pin_1, J5.PWR, R2.Pin_1, Part1.VIN, U2.input_voltage
